// Digital circuit B400.dig as structural Verilog
module B400 (
  input  E,
  input  CLK,
  input  RESET,
  input  I0,
  input  I1,
  input  I2,
  input  I3,
  input  D0,
  input  D1,
  input  D2,
  input  D3,
  input  D4,
  input  D5,
  input  D6,
  input  D7,
  input  GND,
  input  VCC,
  input  P,
  output A0,
  output A1,
  output A2,
  output A3,
  output A4,
  output A5,
  output A6,
  output A7,
  output R0,
  output R1,
  output R2,
  output R3,
  output R4,
  output R5,
  output R6,
  output R7,
  output A_lt_B,
  output A_eq_B,
  output A_gt_B
);

  wire control_unit_1_y0, control_unit_1_y1, control_unit_1_y2, control_unit_1_y3, control_unit_1_y4,
       input_interface_1_b0, input_interface_1_b1, input_interface_1_b2, input_interface_1_b3,
       input_interface_1_y0, input_interface_1_y1, input_interface_1_y2, input_interface_1_y3,
       input_interface_1_y4, input_interface_1_y5, input_interface_1_y6, input_interface_1_y7;

  PROGRAM_COUNTER program_counter_1 (
    .VCC(VCC), .GND(GND), .E(E), .CLK(CLK), .RESET(RESET), .Q0(A0), .Q1(A1), .Q2(A2), .Q3(A3), .Q4(A4),
    .Q5(A5), .Q6(A6), .Q7(A7));
  INPUT_INTERFACE input_interface_1 (
    .A0(I0), .A1(I1), .A2(I2), .A3(I3), .X0(D0), .X1(D1), .X2(D2), .X3(D3), .X4(D4), .X5(D5), .X6(D6),
    .X7(D7), .GND(GND), .VCC(VCC), .OE(P), .B0(input_interface_1_b0), .B1(input_interface_1_b1),
    .B2(input_interface_1_b2), .B3(input_interface_1_b3), .Y0(input_interface_1_y0),
    .Y1(input_interface_1_y1), .Y2(input_interface_1_y2), .Y3(input_interface_1_y3),
    .Y4(input_interface_1_y4), .Y5(input_interface_1_y5), .Y6(input_interface_1_y6), .Y7(input_interface_1_y7));
  RAM_UNIT ram_unit_1 (
    .VCC(VCC), .WE(P), .A0(A0), .A1(A1), .A2(A2), .A3(A3), .A4(A4), .A5(A5), .A6(A6), .A7(A7), .GND(GND),
    .D0(input_interface_1_b0), .D1(input_interface_1_b1), .D2(input_interface_1_b2),
    .D3(input_interface_1_b3), .D4(GND), .D5(GND), .D6(GND), .D7(GND));
  CONTROL_UNIT control_unit_1 (
    .VCC(VCC), .GND(GND), .X0(input_interface_1_b0), .X1(input_interface_1_b1), .X2(input_interface_1_b2),
    .Y0(control_unit_1_y0), .Y1(control_unit_1_y1), .Y2(control_unit_1_y2), .Y3(control_unit_1_y3),
    .Y4(control_unit_1_y4));
  RAM_UNIT ram_unit_2 (
    .VCC(VCC), .WE(P), .A0(A0), .A1(A1), .A2(A2), .A3(A3), .A4(A4), .A5(A5), .A6(A6), .A7(A7), .GND(GND),
    .D0(input_interface_1_y0), .D1(input_interface_1_y1), .D2(input_interface_1_y2),
    .D3(input_interface_1_y3), .D4(input_interface_1_y4), .D5(input_interface_1_y5),
    .D6(input_interface_1_y6), .D7(input_interface_1_y7));
  ALU alu_1 (
    .VCC(VCC), .ADD(control_unit_1_y0), .SUB(control_unit_1_y1), .MUL(control_unit_1_y2),
    .COM(control_unit_1_y3), .EXT(control_unit_1_y4), .A0(input_interface_1_y0), .A1(input_interface_1_y1),
    .A2(input_interface_1_y2), .A3(input_interface_1_y3), .B0(input_interface_1_y4),
    .B1(input_interface_1_y5), .B2(input_interface_1_y6), .B3(input_interface_1_y7), .GND(GND), .R0(R0),
    .R1(R1), .R2(R2), .R3(R3), .R4(R4), .R5(R5), .R6(R6), .R7(R7), .A_lt_B(A_lt_B), .A_eq_B(A_eq_B),
    .A_gt_B(A_gt_B));
endmodule
