// Digital circuit 4-bit Adder.dig as structural Verilog
module _4_bit_Adder (
  input  A0,
  input  A1,
  input  A2,
  input  A3,
  input  B0,
  input  B1,
  input  B2,
  input  B3,
  input  GND,
  input  VCC,
  output S0,
  output S1,
  output S2,
  output S3,
  output C
);

  _74283 _74283_1 (
    .pin1(S1), .pin2(B1), .pin3(A1), .pin4(S0), .pin5(A0), .pin6(B0), .pin7(GND), .pin8(GND), .pin9(C),
    .pin10(S3), .pin11(B3), .pin12(A3), .pin13(S2), .pin14(A2), .pin15(B2), .pin16(VCC));
endmodule
