// Digital circuit CONTROL_UNIT.dig as structural Verilog
module CONTROL_UNIT (
  input  VCC,
  input  GND,
  input  X0,
  input  X1,
  input  X2,
  output Y0,
  output Y1,
  output Y2,
  output Y3,
  output Y4
);

  _74138 _74138_1 (
    .pin1(X0), .pin2(X1), .pin3(X2), .pin4(GND), .pin5(GND), .pin6(VCC), .pin8(GND), .pin10(Y4), .pin11(Y3),
    .pin12(Y2), .pin13(Y1), .pin14(Y0), .pin16(VCC));  // open: pin7, pin9, pin15
endmodule
