// Digital circuit ADDER.dig as structural Verilog
module ADDER (
  input  E,
  input  A0,
  input  A1,
  input  A2,
  input  A3,
  input  B0,
  input  B1,
  input  B2,
  input  B3,
  input  VCC,
  input  GND,
  output R0,
  output R1,
  output R2,
  output R3,
  output R4
);

  wire _74283_1_pin1, _74283_1_pin4, _74283_1_pin9, _74283_1_pin10, _74283_1_pin13;

  _74283 _74283_1 (
    .pin1(_74283_1_pin1), .pin2(B1), .pin3(A1), .pin4(_74283_1_pin4), .pin5(A0), .pin6(B0), .pin7(GND),
    .pin8(GND), .pin9(_74283_1_pin9), .pin10(_74283_1_pin10), .pin11(B3), .pin12(A3), .pin13(_74283_1_pin13),
    .pin14(A2), .pin15(B2), .pin16(VCC));
  _74245 _74245_1 (
    .pin1(VCC), .pin2(_74283_1_pin4), .pin3(_74283_1_pin1), .pin4(_74283_1_pin13), .pin5(_74283_1_pin10),
    .pin6(_74283_1_pin9), .pin7(GND), .pin8(GND), .pin9(GND), .pin10(GND), .pin14(R4), .pin15(R3),
    .pin16(R2), .pin17(R1), .pin18(R0), .pin19(E), .pin20(VCC));  // open: pin11, pin12, pin13
endmodule
