// Digital circuit ALU.dig as structural Verilog
module ALU (
  input  VCC,
  input  ADD,
  input  SUB,
  input  MUL,
  input  COM,
  input  EXT,
  input  A0,
  input  A1,
  input  A2,
  input  A3,
  input  B0,
  input  B1,
  input  B2,
  input  B3,
  input  GND,
  output R0,
  output R1,
  output R2,
  output R3,
  output R4,
  output R5,
  output R6,
  output R7,
  output A_lt_B,
  output A_eq_B,
  output A_gt_B
);

  ADDER adder_1 (
    .E(ADD), .A0(A0), .A1(A1), .A2(A2), .A3(A3), .B0(B0), .B1(B1), .B2(B2), .B3(B3), .VCC(VCC), .GND(GND),
    .R0(R0), .R1(R1), .R2(R2), .R3(R3), .R4(R4));
  SUBTRACTOR subtractor_1 (
    .A0(A0), .A1(A1), .A2(A2), .A3(A3), .B0(B0), .B1(B1), .B2(B2), .B3(B3), .VCC(VCC), .GND(GND), .E(SUB),
    .R0(R0), .R1(R1), .R2(R2), .R3(R3));
  MULTIPLIER multiplier_1 (
    .A0(A0), .A1(A1), .A2(A2), .A3(A3), .E(MUL), .B0(B0), .B1(B1), .B2(B2), .B3(B3), .VCC(VCC), .GND(GND),
    .R0(R0), .R1(R1), .R2(R2), .R3(R3), .R4(R4), .R5(R5), .R6(R6), .R7(R7));
  EXTERNAL external_1 (
    .VCC(VCC), .E(EXT), .A0(A0), .A1(A1), .A2(A2), .A3(A3), .A4(B0), .A5(B1), .A6(B2), .A7(B3), .GND(GND),
    .B0(R0), .B1(R1), .B2(R2), .B3(R3), .B4(R4), .B5(R5), .B6(R6), .B7(R7));
  COMPARATOR comparator_1 (
    .A0(A0), .A1(A1), .A2(A2), .A3(A3), .B0(B0), .B1(B1), .B2(B2), .B3(B3), .E(COM), .VCC(VCC), .GND(GND),
    .A_lt_B(A_lt_B), .A_eq_B(A_eq_B), .A_gt_B(A_gt_B));
endmodule
