// Digital circuit COMPARATOR.dig as structural Verilog
module COMPARATOR (
  input  A0,
  input  A1,
  input  A2,
  input  A3,
  input  B0,
  input  B1,
  input  B2,
  input  B3,
  input  E,
  input  VCC,
  input  GND,
  output A_lt_B,
  output A_eq_B,
  output A_gt_B
);

  wire _7485_1_pin5, _7485_1_pin6, _7485_1_pin7;

  _7485 _7485_1 (
    .pin1(B3), .pin2(GND), .pin3(VCC), .pin4(GND), .pin5(_7485_1_pin5), .pin6(_7485_1_pin6),
    .pin7(_7485_1_pin7), .pin8(GND), .pin9(B0), .pin10(A0), .pin11(B1), .pin12(A1), .pin13(A2), .pin14(B2),
    .pin15(A3), .pin16(VCC));
  _74245 _74245_1 (
    .pin1(VCC), .pin2(_7485_1_pin7), .pin3(_7485_1_pin6), .pin4(_7485_1_pin5), .pin5(GND), .pin6(GND),
    .pin7(GND), .pin8(GND), .pin9(GND), .pin10(GND), .pin16(A_gt_B), .pin17(A_eq_B), .pin18(A_lt_B),
    .pin19(E), .pin20(VCC));  // open: pin11, pin12, pin13, pin14, pin15
endmodule
