// Digital circuit EXTERNAL.dig as structural Verilog
module EXTERNAL (
  input  VCC,
  input  E,
  input  A0,
  input  A1,
  input  A2,
  input  A3,
  input  A4,
  input  A5,
  input  A6,
  input  A7,
  input  GND,
  output B0,
  output B1,
  output B2,
  output B3,
  output B4,
  output B5,
  output B6,
  output B7
);

  _74245 _74245_1 (
    .pin1(VCC), .pin2(A0), .pin3(A1), .pin4(A2), .pin5(A3), .pin6(A4), .pin7(A5), .pin8(A6), .pin9(A7),
    .pin10(GND), .pin11(B7), .pin12(B6), .pin13(B5), .pin14(B4), .pin15(B3), .pin16(B2), .pin17(B1),
    .pin18(B0), .pin19(E), .pin20(VCC));
endmodule
