// Digital circuit INPUT_INTERFACE.dig as structural Verilog
module INPUT_INTERFACE (
  input  A0,
  input  A1,
  input  A2,
  input  A3,
  input  X0,
  input  X1,
  input  X2,
  input  X3,
  input  X4,
  input  X5,
  input  X6,
  input  X7,
  input  GND,
  input  VCC,
  input  OE,
  output B0,
  output B1,
  output B2,
  output B3,
  output Y0,
  output Y1,
  output Y2,
  output Y3,
  output Y4,
  output Y5,
  output Y6,
  output Y7
);

  _74245 _74245_1 (
    .pin1(VCC), .pin2(A0), .pin3(A1), .pin4(A2), .pin5(A3), .pin6(X0), .pin7(X1), .pin8(X2), .pin9(X3),
    .pin10(GND), .pin11(Y3), .pin12(Y2), .pin13(Y1), .pin14(Y0), .pin15(B3), .pin16(B2), .pin17(B1),
    .pin18(B0), .pin19(OE), .pin20(VCC));
  _74245 _74245_2 (
    .pin1(VCC), .pin2(X4), .pin3(X5), .pin4(X6), .pin5(X7), .pin6(GND), .pin7(GND), .pin8(GND), .pin9(GND),
    .pin10(GND), .pin15(Y7), .pin16(Y6), .pin17(Y5), .pin18(Y4), .pin19(OE), .pin20(VCC));  // open: pin11, pin12, pin13, pin14
endmodule
