// Digital circuit MULTIPLIER.dig as structural Verilog
module MULTIPLIER (
  input  A0,
  input  A1,
  input  A2,
  input  A3,
  input  E,
  input  B0,
  input  B1,
  input  B2,
  input  B3,
  input  VCC,
  input  GND,
  output R0,
  output R1,
  output R2,
  output R3,
  output R4,
  output R5,
  output R6,
  output R7
);

  wire multiplier_block_1_c0, multiplier_block_1_c1, multiplier_block_1_c2, multiplier_block_1_c3,
       multiplier_block_1_c4, multiplier_block_1_c5, multiplier_block_1_c6, multiplier_block_1_c7;

  multiplier_block multiplier_block_1 (
    .A0(A0), .A1(A1), .A2(A2), .A3(A3), .B0(B0), .GND(GND), .B1(B1), .VCC(VCC), .B2(B2), .B3(B3),
    .C0(multiplier_block_1_c0), .C1(multiplier_block_1_c1), .C2(multiplier_block_1_c2),
    .C3(multiplier_block_1_c3), .C4(multiplier_block_1_c4), .C5(multiplier_block_1_c5),
    .C6(multiplier_block_1_c6), .C7(multiplier_block_1_c7));
  _74245 _74245_1 (
    .pin1(VCC), .pin2(multiplier_block_1_c0), .pin3(multiplier_block_1_c1), .pin4(multiplier_block_1_c2),
    .pin5(multiplier_block_1_c3), .pin6(multiplier_block_1_c4), .pin7(multiplier_block_1_c5),
    .pin8(multiplier_block_1_c6), .pin9(multiplier_block_1_c7), .pin10(GND), .pin11(R7), .pin12(R6),
    .pin13(R5), .pin14(R4), .pin15(R3), .pin16(R2), .pin17(R1), .pin18(R0), .pin19(E), .pin20(VCC));
endmodule
