// Digital circuit PROGRAM_COUNTER.dig as structural Verilog
module PROGRAM_COUNTER (
  input  VCC,
  input  GND,
  input  E,
  input  CLK,
  input  RESET,
  output Q0,
  output Q1,
  output Q2,
  output Q3,
  output Q4,
  output Q5,
  output Q6,
  output Q7
);

  _74590 _74590_1 (
    .pin1(Q1), .pin2(Q2), .pin3(Q3), .pin4(Q4), .pin5(Q5), .pin6(Q6), .pin7(Q7), .pin8(GND), .pin10(RESET),
    .pin11(CLK), .pin12(E), .pin13(CLK), .pin14(E), .pin15(Q0), .pin16(VCC));  // open: pin9
endmodule
