// Digital circuit RAM.dig as structural Verilog
module RAM (
  input  A0,
  input  A1,
  input  A2,
  input  A3,
  input  A4,
  input  A5,
  input  A6,
  input  A7,
  input  VCC,
  input  GND,
  input  WE,
  input  D0,
  input  D1,
  input  D2,
  input  D3,
  input  D4,
  input  D5,
  input  D6,
  input  D7
);

  // A623308A a623308a_1: pin names not known; wires that end beside it: GND, A7, A6, A5, A4, A3, A2, A1, A0, D0, D1, D2, GND, VCC, WE, GND, GND, GND, GND, GND, GND, D7
endmodule
