// Digital circuit RAM_UNIT.dig as structural Verilog
module RAM_UNIT (
  input  VCC,
  input  WE,
  input  A0,
  input  A1,
  input  A2,
  input  A3,
  input  A4,
  input  A5,
  input  A6,
  input  A7,
  input  GND,
  output D0,
  output D1,
  output D2,
  output D3,
  output D4,
  output D5,
  output D6,
  output D7
);

  wire _74245_1_pin2, _74245_1_pin3, _74245_1_pin4, _74245_1_pin5, _74245_1_pin6, _74245_1_pin7,
       _74245_1_pin8, _74245_1_pin9;

  RAM ram_1 (
    .VCC(VCC), .A0(A0), .A1(A1), .A2(A2), .A3(A3), .A4(A4), .A5(A5), .A6(A6), .A7(A7), .GND(GND), .WE(WE),
    .D0(_74245_1_pin2), .D1(_74245_1_pin3), .D2(_74245_1_pin4), .D3(_74245_1_pin5), .D4(_74245_1_pin6),
    .D5(_74245_1_pin7), .D6(_74245_1_pin8), .D7(_74245_1_pin9));
  _74245 _74245_1 (
    .pin1(WE), .pin2(_74245_1_pin2), .pin3(_74245_1_pin3), .pin4(_74245_1_pin4), .pin5(_74245_1_pin5),
    .pin6(_74245_1_pin6), .pin7(_74245_1_pin7), .pin8(_74245_1_pin8), .pin9(_74245_1_pin9), .pin10(GND),
    .pin11(D7), .pin12(D6), .pin13(D5), .pin14(D4), .pin15(D3), .pin16(D2), .pin17(D1), .pin18(D0),
    .pin19(GND), .pin20(VCC));
endmodule
