// Digital circuit SUBTRACTOR.dig as structural Verilog
module SUBTRACTOR (
  input  A0,
  input  A1,
  input  A2,
  input  A3,
  input  B0,
  input  B1,
  input  B2,
  input  B3,
  input  VCC,
  input  GND,
  input  E,
  output R0,
  output R1,
  output R2,
  output R3
);

  wire _74283_1_pin1, _74283_1_pin4, _74283_1_pin10, _74283_1_pin13, adder_1_r0, adder_1_r1, adder_1_r2,
       adder_1_r3, not_1_out, not_2_out, not_3_out, not_4_out;

  not not_1 (not_1_out, B0);
  not not_2 (not_2_out, B1);
  not not_3 (not_3_out, B2);
  not not_4 (not_4_out, B3);
  _74283 _74283_1 (
    .pin1(_74283_1_pin1), .pin2(not_2_out), .pin3(A1), .pin4(_74283_1_pin4), .pin5(A0), .pin6(not_1_out),
    .pin7(GND), .pin8(GND), .pin10(_74283_1_pin10), .pin11(not_4_out), .pin12(A3), .pin13(_74283_1_pin13),
    .pin14(A2), .pin15(not_3_out), .pin16(VCC));  // open: pin9
  ADDER adder_1 (
    .E(E), .A0(_74283_1_pin4), .A1(_74283_1_pin1), .A2(_74283_1_pin13), .A3(_74283_1_pin10), .B0(VCC),
    .B1(GND), .B2(GND), .B3(GND), .VCC(VCC), .GND(GND), .R0(adder_1_r0), .R1(adder_1_r1), .R2(adder_1_r2),
    .R3(adder_1_r3));  // open: R4
  _74245 _74245_1 (
    .pin1(VCC), .pin2(adder_1_r0), .pin3(adder_1_r1), .pin4(adder_1_r2), .pin5(adder_1_r3), .pin6(GND),
    .pin7(GND), .pin8(GND), .pin9(GND), .pin10(GND), .pin15(R3), .pin16(R2), .pin17(R1), .pin18(R0),
    .pin19(E), .pin20(VCC));  // open: pin11, pin12, pin13, pin14
endmodule
