// Digital circuit multiplier_block.dig as structural Verilog
module multiplier_block (
  input  A0,
  input  A1,
  input  A2,
  input  A3,
  input  B0,
  input  GND,
  input  B1,
  input  VCC,
  input  B2,
  input  B3,
  output C0,
  output C1,
  output C2,
  output C3,
  output C4,
  output C5,
  output C6,
  output C7
);

  wire _4_bit_adder_2_c, _4_bit_adder_2_s1, _4_bit_adder_2_s2, _4_bit_adder_2_s3, _4_bit_adder_3_c,
       _4_bit_adder_3_s1, _4_bit_adder_3_s2, _4_bit_adder_3_s3, and_1_out, and_2_out, and_3_out, and_4_out,
       and_5_out, and_6_out, and_7_out, and_8_out, and_9_out, and_10_out, and_11_out, and_12_out, and_13_out,
       and_14_out, and_15_out;

  and and_1 (and_1_out, A3, B2);
  and and_2 (and_2_out, A3, B3);
  and and_3 (and_3_out, A3, B1);
  and and_4 (and_4_out, A2, B2);
  and and_5 (and_5_out, A2, B3);
  and and_6 (and_6_out, A2, B1);
  and and_7 (and_7_out, A1, B2);
  and and_8 (and_8_out, A1, B3);
  and and_9 (and_9_out, A1, B1);
  and and_10 (and_10_out, A0, B2);
  and and_11 (and_11_out, A0, B3);
  and and_12 (and_12_out, A0, B1);
  and and_13 (and_13_out, A3, B0);
  and and_14 (and_14_out, A2, B0);
  _4_bit_Adder _4_bit_adder_1 (
    .A0(_4_bit_adder_3_s1), .A1(_4_bit_adder_3_s2), .A2(_4_bit_adder_3_s3), .A3(_4_bit_adder_3_c),
    .B0(and_11_out), .B1(and_8_out), .B2(and_5_out), .B3(and_2_out), .GND(GND), .VCC(VCC), .S0(C3), .S1(C4),
    .S2(C5), .S3(C6), .C(C7));
  and and_15 (and_15_out, A1, B0);
  _4_bit_Adder _4_bit_adder_2 (
    .A0(and_15_out), .A1(and_14_out), .A2(and_13_out), .A3(GND), .B0(and_12_out), .B1(and_9_out),
    .B2(and_6_out), .B3(and_3_out), .GND(GND), .VCC(VCC), .S0(C1), .S1(_4_bit_adder_2_s1),
    .S2(_4_bit_adder_2_s2), .S3(_4_bit_adder_2_s3), .C(_4_bit_adder_2_c));
  _4_bit_Adder _4_bit_adder_3 (
    .A0(_4_bit_adder_2_s1), .A1(_4_bit_adder_2_s2), .A2(_4_bit_adder_2_s3), .A3(_4_bit_adder_2_c),
    .B0(and_10_out), .B1(and_7_out), .B2(and_4_out), .B3(and_1_out), .GND(GND), .VCC(VCC), .S0(C2),
    .S1(_4_bit_adder_3_s1), .S2(_4_bit_adder_3_s2), .S3(_4_bit_adder_3_s3), .C(_4_bit_adder_3_c));
  and and_16 (C0, A0, B0);
endmodule
